# Fritzing sketch Reciever (saved by Fritzing 0.9.3b)
breadboards: 1

parts:
  Part1 = Arduino Mega ADK (Rev3)
  Part3 = NRF24L01

nets:
  N1: Part1.D8_PWM, Part3.CSN
  3V3: Part1.3V3, Part3.VCC
  GND: Part1.GND, Part3.GND
  N2: Part1.D7_PWM, Part3.CE
  N3: Part1.D50/MISO, Part3.MISO
  N4: Part1.D51/MOSI, Part3.MOSI
  N5: Part1.D52/SCK, Part3.SCK
